# Fritzing sketch line_follower (saved by Fritzing 0.9.10b)
breadboards: 1

parts:
  Part1 = Arduino Nano (Rev3.0)
  IC1 = Voltage Regulator [package=to220-igo]
  BAT1 = BC9VPC [package=bc9vpc]
  IC2 = L293D [package=THT]
  U1 = LIPO-2000mAh [package=lipo-2000]
  M1 = DC Motor [voltage_(max)=6V voltage_(min)=3V]
  M2 = DC Motor [voltage_(max)=6V voltage_(min)=3V]
  Q1 = PHOTOTRANSISTOR REFLECTIVE OBJECT SENSOR [package=qrb1114-side]
  Q2 = PHOTOTRANSISTOR REFLECTIVE OBJECT SENSOR [package=qrb1114-side]
  Q3 = PHOTOTRANSISTOR REFLECTIVE OBJECT SENSOR [package=qrb1114-side]
  Q4 = PHOTOTRANSISTOR REFLECTIVE OBJECT SENSOR [package=qrb1114-side]
  Q5 = PHOTOTRANSISTOR REFLECTIVE OBJECT SENSOR [package=qrb1114-side]
  Q6 = PHOTOTRANSISTOR REFLECTIVE OBJECT SENSOR [package=qrb1114-side]
  R1 = Resistor [tolerance=±5% resistance=4.7k package=THT]
  R2 = Resistor [tolerance=±5% resistance=4.7k power=0.25 package=THT]
  R3 = Resistor [tolerance=±5% resistance=4.7k power=0.25 package=THT]
  R4 = Resistor [tolerance=±5% resistance=4.7k power=0.25 package=THT]
  R5 = Resistor [tolerance=±5% resistance=4.7k power=0.25 package=THT]
  R6 = Resistor [tolerance=±5% resistance=4.7k power=0.25 package=THT]
  R7 = Resistor [tolerance=±5% resistance=10 package="2010 [SMD]"]
  Q7 = PHOTOTRANSISTOR REFLECTIVE OBJECT SENSOR [package=qrb1114-side]
  Q8 = PHOTOTRANSISTOR REFLECTIVE OBJECT SENSOR [package=qrb1114-side]
  R8 = Resistor [tolerance=±5% resistance=4.7k power=0.25 package=THT]
  R9 = Resistor [tolerance=±5% resistance=4.7k power=0.25 package=THT]
  R10 = Resistor [tolerance=±5% resistance=10 package="2010 [SMD]"]

nets:
  GND: Part1.GND, IC1.GND, BAT1.V-, IC2.0V, U1.-, Q1.K, Q2.K, Q3.K, Q4.K, Q5.K, Q6.K, R1.Pin_1, R2.Pin_1, R3.Pin_1, R4.Pin_1, R5.Pin_1, R6.Pin_1, Q7.K, Q8.K, R8.Pin_1, R9.Pin_1
  N1: Part1.D3, IC2.In_3
  N2: Part1.D5, IC2.In_4
  N3: Part1.D6, IC2.In_2
  N4: Part1.D9, IC2.In_1
  N5: Part1.VIN, IC1.OUT, IC2.Enable_1, IC2.Enable_2, IC2.+V, Q1.C, Q2.C, Q3.C, Q4.C, Q5.C, Q6.C, R7.Pin_0, Q7.C, Q8.C, R10.Pin_0
  N6: Part1.A7, Q8.E, R9.Pin_0
  N7: Part1.A6, Q7.E, R8.Pin_0
  N8: Part1.A5, Q6.E, R6.Pin_0
  N9: Part1.A4, Q5.E, R5.Pin_0
  N10: Part1.A3, Q4.E, R4.Pin_0
  N11: Part1.A2, Q3.E, R3.Pin_0
  N12: Part1.A1, Q2.E, R2.Pin_0
  N13: Part1.A0, Q1.E, R1.Pin_0
  N14: IC1.IN, BAT1.V+
  N15: IC2.Out_1_(_Controlled_by_Enable_1_), M2.pin_2
  N16: IC2.Out_2_(_Controlled_by_Enable_1_), M2.pin_1
  N17: IC2.+Vmotor, U1.+
  N18: IC2.Out_3_(_Controlled_by_Enable_2_), M1.pin_2
  N19: IC2.Out_4_(_Controlled_by_Enable_2_), M1.pin_1
  N20: Q1.A, Q2.A, Q3.A, Q4.A, R7.Pin_1
  N21: Q5.A, Q6.A, Q7.A, Q8.A, R10.Pin_1
